# Fritzing sketch programmer (saved by Fritzing 0.9.3b)
circuit board: 5.33256cm x 7.87467cm
breadboards: 1
perfboards: 1

parts:
  U2 = Voltage Regulator [package=to220-adj]
  R1 = Resistor [tolerance=±5% resistance=150 package=THT]
  R2 = Resistor [tolerance=±5% resistance=2k package=THT]
  D1 = Rectifier Diode [part_number=1N4001 breakdown_voltage=3.6V package="300 mil [THT]"]
  C4 = Electrolytic Capacitor [capacitance=100µF package="100 mil [THT, electrolytic]"]
  U3 = Voltage Regulator [package=to220-adj]
  R3 = Resistor [tolerance=±5% resistance=200 package=THT]
  R4 = Resistor [tolerance=±5% resistance=680 package=THT]
  C9 = Electrolytic Capacitor [capacitance=100µF package="100 mil [THT, electrolytic]"]
  D3 = Rectifier Diode [part_number=1N4001 breakdown_voltage=3.6V package="300 mil [THT]"]
  J1 = Power Jack [package=power_jack_pth_lock]
  IC1 = MICROCONTROLLER [package=dil28-3-simon]
  U4 = Voltage Regulator [package=to220-adj]
  R5 = Resistor [tolerance=±5% resistance=150 package=THT]
  R6 = Resistor [tolerance=±5% resistance=2.4k package=THT]
  C14 = Electrolytic Capacitor [capacitance=100µF package="100 mil [THT, electrolytic]"]
  D4 = Rectifier Diode [part_number=1N4001 breakdown_voltage=3.6V package="300 mil [THT]"]
  C16 = Ceramic Capacitor [capacitance=100nF package="100 mil [THT, multilayer]"]
  D5 = Rectifier Diode [part_number=1N4148 package="300 mil [THT]"]
  R7 = Resistor [tolerance=±5% resistance=4.7k package=THT]
  R8 = Resistor [tolerance=±5% resistance=1k package=THT]
  C17 = Ceramic Capacitor [capacitance=100nF package="100 mil [THT, multilayer]"]
  D6 = Rectifier Diode [part_number=1N4001 package="300 mil [THT]"]
  R10 = Resistor [tolerance=±5% resistance=10k package=THT]
  C18 = Ceramic Capacitor [capacitance=100nF package="100 mil [THT, multilayer]"]
  J3 = female pin header, 3 pins [form="♀ (female)"]
  D7 = Rectifier Diode [part_number=1N4148 package="300 mil [THT]"]
  R11 = Resistor [tolerance=±5% resistance=4.7k package=THT]
  R12 = Resistor [tolerance=±5% resistance=1k package=THT]
  R13 = Resistor [tolerance=±5% resistance=1k package=THT]
  XTAL1 = Crystal [frequency="4 MHz" package=THT]
  C19 = Ceramic Capacitor [capacitance=22pF package="100 mil [THT, multilayer]"]
  C20 = Ceramic Capacitor [capacitance=22pF package="100 mil [THT, multilayer]"]
  C21 = Ceramic Capacitor [capacitance=100nF package="100 mil [THT, multilayer]"]
  D8 = Rectifier Diode [part_number=1N4001 package="300 mil [THT]"]
  C15 = Electrolytic Capacitor [capacitance=1mF package="200 mil [THT, electrolytic]"]
  8742 = Intel 8742 [package="DIP (Dual Inline) [THT]"]
  J4 = female pin header, 5 pins [form="♀ (female)"]
  R9 = Resistor [tolerance=±5% resistance=1k package=THT]
  R14 = Resistor [tolerance=±5% resistance=1k package=THT]
  R15 = Resistor [tolerance=±5% resistance=1k package=THT]
  Q4 = PNP-Transistor [package="TO92 [THT]"]
  Q2 = PNP-Transistor [package="TO92 [THT]"]
  Q1 = NPN-Transistor [part_number=BC550 package="TO92 [THT]"]
  Q3 = NPN-Transistor [part_number=BC550 package="TO92 [THT]"]
  D9 = Rectifier Diode [part_number=1N4148 package="300 mil [THT]"]
  Q5 = NPN-Transistor [part_number=BC550 package="TO92 [THT]"]
  Q6 = PNP-Transistor [part_number=BC327 package="TO92 [THT]"]
  R16 = Resistor [tolerance=±5% resistance=4.7k package=THT]
  R17 = Resistor [tolerance=±5% resistance=1k package=THT]
  R18 = Resistor [tolerance=±5% resistance=1k package=THT]
  R19 = Resistor [tolerance=±5% resistance=1k package=THT]
  XTAL2 = Crystal [frequency="16 Mhz" package=THT]
  C22 = Ceramic Capacitor [capacitance=100nF package="100 mil [THT, multilayer]"]
  C23 = Ceramic Capacitor [capacitance=100nF package="100 mil [THT, multilayer]"]

nets:
  N1: U2.ADJ, R1.Pin_0, R2.Pin_0
  24V: U2.IN, D1.cathode, U3.IN, D3.cathode, J1.PWR, U4.IN, D4.cathode, C16.1, C15.+
  18V: U2.OUT, R1.Pin_1, D1.anode, C4.+, R7.Pin_0, Q2.E, Q6.E, R16.Pin_0
  GND: R2.Pin_1, C4.-, R4.Pin_1, C9.-, J1.GND, IC1.GND, IC1.AGND, R6.Pin_1, C14.-, C16.0, C17.0, C18.0, J3.pin1, R13.Pin_1, C19.0, C20.0, C21.0, C15.-, 8742.VSS, J4.pin5, R9.Pin_1, Q1.E, Q3.E, Q5.E, R18.Pin_1, C22.1, C23.1
  N2: U3.ADJ, R3.Pin_0, R4.Pin_0
  5.5V: U3.OUT, R3.Pin_1, C9.+, D3.anode, D5.anode, D6.anode, D7.anode, D8.anode, D9.anode
  AT_RESET: IC1.PC6(_RESET), R10.Pin_1, J4.pin4
  AT_RX: IC1.PD0(RXD), J3.pin3
  AT_TX: IC1.PD1(TXD), J3.pin2
  DB0: IC1.PD2(INT0), 8742.D0
  DB1: IC1.PD3(INT1), 8742.D1
  DB2: IC1.PD4(XCK_T0), 8742.D2
  N3: IC1.VCC, IC1.AVCC, D6.cathode, R10.Pin_0, C18.1
  N4: IC1.PB6(XTAL1_TOSC1), XTAL2.pin_1, C22.0
  N5: IC1.PB7(XTAL2_TOSC2), XTAL2.pin_0, C23.0
  P22: IC1.PD6(AIN0), 8742.P22
  P21: IC1.PD7(AIN1), 8742.P21
  P20: IC1.PB0(ICP), 8742.P20
  DB7: IC1.PB1(OC1A), 8742.D7
  DB6: IC1.PB2(SS_OC1B), 8742.D6
  DB5: IC1.PB3(MOSI_OC2), 8742.D5, J4.pin1
  DB4: IC1.PB4(MISO), 8742.D4, J4.pin2
  DB3: IC1.PB5(SCK), 8742.D3, J4.pin3
  N6: IC1.AREF, C17.1
  N7: IC1.PC0(ADC0), R15.Pin_1
  N8: IC1.PC1(ADC1), R14.Pin_1
  RESET: IC1.PC2(ADC2), 8742.!RESET
  TEST0: IC1.PC3(ADC3), 8742.TEST0
  N9: IC1.PC4(ADC4_SDA), R19.Pin_1
  N10: U4.ADJ, R5.Pin_0, R6.Pin_0
  21V: U4.OUT, R5.Pin_1, C14.+, D4.anode, R11.Pin_0, Q4.E
  PROG: D5.cathode, 8742.PROG, R9.Pin_0, Q2.C
  N11: R7.Pin_1, R8.Pin_0, Q2.B
  N12: R8.Pin_1, Q1.C
  VDD: D7.cathode, R13.Pin_0, 8742.VDD, Q4.C
  N13: R11.Pin_1, R12.Pin_0, Q4.B
  N14: R12.Pin_1, Q3.C
  N15: XTAL1.pin_0, C19.1, 8742.XTAL1
  N16: XTAL1.pin_1, C20.1, 8742.XTAL2
  N17: C21.1, D8.cathode, 8742.VCC
  EA: 8742.EA, D9.cathode, Q6.C, R18.Pin_0
  N18: R14.Pin_0, Q1.B
  N19: R15.Pin_0, Q3.B
  N20: Q5.B, R19.Pin_0
  N21: Q5.C, R17.Pin_1
  N22: Q6.B, R16.Pin_1, R17.Pin_0

custom parts:
  Intel 8742: MCS-48
